// Logisim project 74IC.circ as structural Verilog: 10 circuits, main circuit 74283
module _74125 (
  input  _1G_tilde,
  input  Vcc,
  input  _1A,
  input  _4G_tilde,
  input  _4A,
  input  _2G_tilde,
  input  _2A,
  input  _3G_tilde,
  input  _3A,
  input  GND,
  output _1Y,
  output _4Y,
  output _2Y,
  output _3Y
);

  wire not_1_out, not_2_out, not_3_out, not_4_out;

  not not_1 (not_1_out, _1G_tilde);
  assign _1Y = not_1_out ? _1A : 1'bz;  // Controlled_Buffer controlled_buffer_1
  not not_2 (not_2_out, _2G_tilde);
  assign _2Y = not_2_out ? _2A : 1'bz;  // Controlled_Buffer controlled_buffer_2
  not not_3 (not_3_out, _4G_tilde);
  assign _4Y = not_3_out ? _4A : 1'bz;  // Controlled_Buffer controlled_buffer_3
  not not_4 (not_4_out, _3G_tilde);
  assign _3Y = not_4_out ? _3A : 1'bz;  // Controlled_Buffer controlled_buffer_4
endmodule

module _74191 (
  input  nCTE,
  input  D_nU,
  input  CK,
  input  nLOAD,
  input  A,
  input  B,
  input  C,
  input  D,
  output MAX_MIN,
  output nRCO,
  output QA,
  output QB,
  output QC,
  output QD
);

  wire and_1_out, and_2_out, and_3_out, and_4_out, and_5_out, and_6_out, d_ff_1_qn, d_ff_2_qn, d_ff_4_qn,
       nand_1_out, nand_2_out, nand_3_out, nand_4_out, nand_5_out, nand_6_out, nand_7_out, nand_8_out,
       nand_9_out, nand_10_out, nand_11_out, nand_12_out, nand_13_out, nand_14_out, nand_15_out, nand_16_out,
       nand_17_out, nand_18_out, nand_19_out, not_1_out, not_2_out, not_3_out, not_4_out, not_5_out,
       not_6_out, not_7_out, not_8_out, not_9_out, not_10_out, not_11_out, not_12_out, not_14_out,
       not_15_out, not_16_out, not_17_out, not_18_out, not_19_out, not_20_out, not_21_out, not_22_out,
       not_23_out, not_24_out, not_25_out, not_26_out, or_2_out, or_3_out, or_4_out, undriven, undriven_2,
       xor_1_out, xor_2_out, xor_3_out, xor_4_out, xor_5_out, xor_6_out, xor_7_out;

  not not_1 (not_1_out, CK);
  not not_2 (not_2_out, nLOAD);
  not not_3 (not_3_out, A);
  not not_4 (not_4_out, B);
  not not_5 (not_5_out, C);
  not not_6 (not_6_out, D);
  not not_7 (not_7_out, D_nU);
  nand nand_1 (nand_1_out, A, not_2_out);
  nand nand_2 (nand_2_out, not_2_out, not_3_out);
  nand nand_3 (nand_3_out, B, not_2_out);
  nand nand_4 (nand_4_out, not_2_out, not_4_out);
  nand nand_5 (nand_5_out, C, not_2_out);
  nand nand_6 (nand_6_out, not_2_out, not_5_out);
  nand nand_7 (nand_7_out, D, not_2_out);
  nand nand_8 (nand_8_out, not_2_out, not_6_out);
  not not_8 (not_8_out, not_7_out);
  and and_1 (and_1_out, ~not_7_out, ~nCTE);  // AND_Gate
  and and_2 (and_2_out, not_15_out, undriven);
  and and_3 (and_3_out, d_ff_1_qn, undriven_2);
  and and_4 (and_4_out, not_15_out, undriven, not_12_out);
  and and_5 (and_5_out, d_ff_1_qn, undriven_2, d_ff_2_qn);
  and and_6 (and_6_out, ~not_8_out, ~nCTE);  // AND_Gate
  xor xor_1 (xor_1_out, not_15_out, not_12_out);
  xor xor_2 (xor_2_out, not_12_out, d_ff_1_qn);
  xor xor_3 (xor_3_out, and_2_out, not_12_out);
  xor xor_4 (xor_4_out, not_12_out, and_3_out);
  xor xor_5 (xor_5_out, and_4_out, not_14_out);
  xor xor_6 (xor_6_out, not_14_out, and_5_out);
  not not_9 (not_9_out, nCTE);
  not not_10 (not_10_out, not_9_out);
  nand nand_9 (nand_9_out, not_15_out, undriven, not_12_out, not_14_out, not_7_out);
  nand nand_10 (nand_10_out, d_ff_1_qn, undriven_2, d_ff_2_qn, d_ff_4_qn, not_8_out);
  not not_11 (not_11_out, nand_1_out);
  nand nand_11 (nand_11_out, and_6_out, xor_1_out);
  nand nand_12 (nand_12_out, not_10_out, not_12_out);
  nand nand_13 (nand_13_out, xor_2_out, and_1_out);
  not not_12 (not_12_out, d_ff_2_qn);
  nand nand_14 (nand_14_out, and_6_out, xor_3_out);
  nand nand_15 (nand_15_out, not_10_out, not_12_out);
  nand nand_16 (nand_16_out, xor_4_out, and_1_out);
  not not_13 (not_12_out, d_ff_2_qn);
  nand nand_17 (nand_17_out, and_6_out, xor_5_out);
  nand nand_18 (nand_18_out, not_10_out, not_14_out);
  nand nand_19 (nand_19_out, xor_6_out, and_1_out);
  not not_14 (not_14_out, d_ff_4_qn);
  or or_1 (MAX_MIN, ~nand_9_out, ~nand_10_out);  // OR_Gate
  xor xor_7 (xor_7_out, not_9_out, not_15_out);
  not not_15 (not_15_out, d_ff_1_qn);
  not not_16 (not_16_out, nand_2_out);
  or or_2 (or_2_out, ~nand_11_out, ~nand_12_out, ~nand_13_out);  // OR_Gate
  not not_17 (not_17_out, nand_3_out);
  not not_18 (not_18_out, nand_4_out);
  or or_3 (or_3_out, ~nand_14_out, ~nand_15_out, ~nand_16_out);  // OR_Gate
  not not_19 (not_19_out, nand_5_out);
  not not_20 (not_20_out, nand_6_out);
  or or_4 (or_4_out, ~nand_17_out, ~nand_18_out, ~nand_19_out);  // OR_Gate
  not not_21 (not_21_out, nand_7_out);
  not not_22 (not_22_out, nand_8_out);
  nand nand_20 (nRCO, MAX_MIN, not_9_out, not_1_out);
  not not_23 (not_23_out, not_1_out);
  D_Flip_Flop #(.trigger("high")) d_ff_1 (
    .clk(not_23_out), .D(xor_7_out), .Q(QA), .Qn(d_ff_1_qn), .preset(not_11_out), .reset(not_16_out));  // open: en
  not not_24 (not_24_out, not_1_out);
  D_Flip_Flop #(.trigger("high")) d_ff_2 (
    .clk(not_24_out), .D(or_2_out), .Q(QB), .Qn(d_ff_2_qn), .preset(not_17_out), .reset(not_18_out));  // open: en
  D_Flip_Flop #(.trigger("high")) d_ff_3 (
    .clk(not_25_out), .D(or_3_out), .Q(QC), .Qn(d_ff_2_qn), .preset(not_19_out), .reset(not_20_out));  // open: en
  not not_25 (not_25_out, not_1_out);
  not not_26 (not_26_out, not_1_out);
  D_Flip_Flop #(.trigger("high")) d_ff_4 (
    .clk(not_26_out), .D(or_4_out), .Q(QD), .Qn(d_ff_4_qn), .preset(not_21_out), .reset(not_22_out));  // open: en
endmodule

module _74257 (
  input  SELECT,
  input  VCC,
  input  nEN,
  input  GND,
  input  _1A_2,
  input  _1B_3,
  input  _2A_5,
  input  _2B_6,
  input  _3A_11,
  input  _3B_12,
  input  _4A_14,
  input  _4B_13,
  output _1Y,
  output _2Y,
  output _3Y,
  output _4Y
);

  wire not_1_out;

  not not_1 (not_1_out, nEN);
  Multiplexer multiplexer_1 (.in0(_1A_2), .in1(_1B_3), .out(_1Y), .sel(SELECT), .en(not_1_out));
  Multiplexer multiplexer_2 (.in0(_2A_5), .in1(_2B_6), .out(_2Y), .sel(SELECT), .en(not_1_out));
  Multiplexer multiplexer_3 (.in0(_3A_11), .in1(_3B_12), .out(_3Y), .sel(SELECT), .en(not_1_out));
  Multiplexer multiplexer_4 (.in0(_4A_14), .in1(_4B_13), .out(_4Y), .sel(SELECT), .en(not_1_out));
endmodule

module _74259 (
  input  S0,
  input  S1,
  input  S2,
  input  G_tilde,
  input  D,
  input  CLR_tilde,
  output Q0,
  output Q1,
  output Q2,
  output Q3,
  output Q4,
  output Q5,
  output Q6,
  output Q7
);

  wire and_1_out, and_2_out, and_3_out, and_4_out, and_5_out, and_6_out, and_7_out, and_8_out, buffer_1_out,
       buffer_2_out, buffer_3_out, nand_1_out, nand_2_out, nand_3_out, nand_4_out, nand_5_out, nand_6_out,
       nand_7_out, nand_8_out, not_1_out, not_2_out, not_3_out, not_4_out, not_5_out, not_6_out, not_7_out,
       not_8_out;

  not not_1 (not_1_out, G_tilde);
  not not_2 (not_2_out, D);
  not not_3 (not_3_out, CLR_tilde);
  not not_4 (not_4_out, S0);
  buf buffer_1 (buffer_1_out, S0);
  not not_5 (not_5_out, S1);
  buf buffer_2 (buffer_2_out, S1);
  not not_6 (not_6_out, S2);
  buf buffer_3 (buffer_3_out, S2);
  not not_7 (not_7_out, not_1_out);
  not not_8 (not_8_out, not_3_out);
  nand nand_1 (nand_1_out, not_4_out, not_5_out, not_6_out);
  nand nand_2 (nand_2_out, buffer_1_out, not_5_out, not_6_out);
  nand nand_3 (nand_3_out, not_4_out, buffer_2_out, not_6_out);
  nand nand_4 (nand_4_out, buffer_1_out, buffer_2_out, not_6_out);
  nand nand_5 (nand_5_out, not_4_out, not_5_out, buffer_3_out);
  nand nand_6 (nand_6_out, buffer_1_out, not_5_out, buffer_3_out);
  nand nand_7 (nand_7_out, not_4_out, buffer_2_out, buffer_3_out);
  nand nand_8 (nand_8_out, buffer_1_out, buffer_2_out, buffer_3_out);
  and and_1 (and_1_out, ~not_7_out, ~nand_1_out);  // AND_Gate
  and and_2 (and_2_out, ~not_7_out, ~nand_2_out);  // AND_Gate
  and and_3 (and_3_out, ~not_7_out, ~nand_3_out);  // AND_Gate
  and and_4 (and_4_out, ~not_7_out, ~nand_4_out);  // AND_Gate
  and and_5 (and_5_out, ~not_7_out, ~nand_5_out);  // AND_Gate
  and and_6 (and_6_out, ~not_7_out, ~nand_6_out);  // AND_Gate
  and and_7 (and_7_out, ~not_7_out, ~nand_7_out);  // AND_Gate
  and and_8 (and_8_out, ~not_7_out, ~nand_8_out);  // AND_Gate
  D_Flip_Flop #(.trigger("high")) d_ff_1 (
    .clk(and_1_out), .D(not_2_out), .Q(Q0), .reset(not_8_out));  // open: Qn, preset, en
  D_Flip_Flop #(.trigger("high")) d_ff_2 (
    .clk(and_2_out), .D(not_2_out), .Q(Q1), .reset(not_8_out));  // open: Qn, preset, en
  D_Flip_Flop #(.trigger("high")) d_ff_3 (
    .clk(and_3_out), .D(not_2_out), .Q(Q2), .reset(not_8_out));  // open: Qn, preset, en
  D_Flip_Flop #(.trigger("high")) d_ff_4 (
    .clk(and_4_out), .D(not_2_out), .Q(Q3), .reset(not_8_out));  // open: Qn, preset, en
  D_Flip_Flop #(.trigger("high")) d_ff_5 (
    .clk(and_5_out), .D(not_2_out), .Q(Q4), .reset(not_8_out));  // open: Qn, preset, en
  D_Flip_Flop #(.trigger("high")) d_ff_6 (
    .clk(and_6_out), .D(not_2_out), .Q(Q5), .reset(not_8_out));  // open: Qn, preset, en
  D_Flip_Flop #(.trigger("high")) d_ff_7 (
    .clk(and_7_out), .D(not_2_out), .Q(Q6), .reset(not_8_out));  // open: Qn, preset, en
  D_Flip_Flop #(.trigger("high")) d_ff_8 (
    .clk(and_8_out), .D(not_2_out), .Q(Q7), .reset(not_8_out));  // open: Qn, preset, en
endmodule

module _74283 (
  input  B4,
  input  A4,
  input  B3,
  input  A3,
  input  B2,
  input  A2,
  input  B1,
  input  A1,
  input  C0,
  output C4,
  output Z4,
  output Z3,
  output Z2,
  output Z1
);

  wire and_1_out, and_2_out, nand_1_out, nand_2_out, nand_3_out, nand_4_out, nand_5_out, nand_6_out,
       nand_7_out, nand_8_out, nand_9_out, nand_10_out, nand_11_out, nand_12_out, nand_13_out, nand_14_out,
       nand_15_out, nand_16_out, nand_17_out, nand_18_out, nand_19_out, nand_20_out, nor_1_out, nor_2_out,
       nor_3_out, nor_4_out, nor_5_out, nor_6_out, nor_7_out, nor_8_out, nor_9_out, nor_10_out, not_1_out,
       not_2_out, not_3_out, not_4_out, not_5_out, not_6_out, not_7_out, not_8_out, not_9_out, not_10_out,
       not_11_out, not_12_out, not_13_out, not_14_out, not_15_out, not_16_out, not_17_out, not_18_out,
       not_19_out, not_20_out, not_21_out, not_22_out, not_23_out, not_24_out, not_25_out, not_26_out,
       not_27_out, not_28_out, not_29_out, not_30_out, not_31_out, xor_1_out, xor_2_out, xor_3_out, xor_4_out;

  not not_1 (not_1_out, B4);
  not not_2 (not_2_out, A4);
  not not_3 (not_3_out, B3);
  not not_4 (not_4_out, A3);
  not not_5 (not_5_out, B2);
  not not_6 (not_6_out, A2);
  not not_7 (not_7_out, B1);
  not not_8 (not_8_out, A1);
  nor nor_1 (nor_1_out, not_1_out, not_2_out);
  nand nand_1 (nand_1_out, not_1_out, not_2_out);
  nor nor_2 (nor_2_out, not_3_out, not_4_out);
  nand nand_2 (nand_2_out, not_3_out, not_4_out);
  nor nor_3 (nor_3_out, not_5_out, not_6_out);
  nand nand_3 (nand_3_out, not_5_out, not_6_out);
  nor nor_4 (nor_4_out, not_7_out, not_8_out);
  nand nand_4 (nand_4_out, not_7_out, not_8_out);
  not not_9 (not_9_out, nor_1_out);
  not not_10 (not_10_out, nand_1_out);
  nor nor_5 (nor_5_out, nor_1_out, nor_2_out);
  not not_11 (not_11_out, nor_2_out);
  not not_12 (not_12_out, nand_2_out);
  not not_13 (not_13_out, nor_3_out);
  not not_14 (not_14_out, nand_3_out);
  nor nor_6 (nor_6_out, nor_3_out, nor_4_out);
  not not_15 (not_15_out, nor_4_out);
  not not_16 (not_16_out, nand_4_out);
  not not_17 (not_17_out, C0);
  and and_1 (and_1_out, not_12_out, not_9_out);
  nand nand_5 (nand_5_out, not_14_out, not_9_out, not_11_out);
  nand nand_6 (nand_6_out, not_16_out, nor_5_out, not_13_out);
  nand nand_7 (nand_7_out, nor_5_out, not_13_out, not_15_out);
  not not_18 (not_18_out, not_17_out);
  not not_19 (not_19_out, not_10_out);
  and and_2 (and_2_out, not_14_out, not_11_out);
  nand nand_8 (nand_8_out, not_16_out, not_11_out, not_13_out);
  nand nand_9 (nand_9_out, not_11_out, nor_6_out, not_17_out);
  not not_20 (not_20_out, not_12_out);
  not not_21 (not_21_out, not_14_out);
  nand nand_10 (nand_10_out, not_16_out, not_13_out);
  nand nand_11 (nand_11_out, nor_6_out, not_17_out);
  not not_22 (not_22_out, not_14_out);
  not not_23 (not_23_out, not_16_out);
  nand nand_12 (nand_12_out, not_15_out, not_17_out);
  not not_24 (not_24_out, not_16_out);
  not not_25 (not_25_out, not_17_out);
  nor nor_7 (nor_7_out, not_10_out, and_1_out);
  nor nor_8 (nor_8_out, not_12_out, and_2_out);
  nand nand_13 (nand_13_out, nor_7_out, nand_5_out, nand_6_out);
  nor nor_9 (nor_9_out, nand_7_out, not_18_out);
  nand nand_14 (nand_14_out, not_9_out, not_19_out);
  nand nand_15 (nand_15_out, nor_8_out, nand_8_out, nand_9_out);
  nand nand_16 (nand_16_out, not_11_out, not_20_out);
  nand nand_17 (nand_17_out, not_21_out, nand_10_out, nand_11_out);
  nand nand_18 (nand_18_out, not_13_out, not_22_out);
  nand nand_19 (nand_19_out, not_23_out, nand_12_out);
  nand nand_20 (nand_20_out, not_15_out, not_24_out);
  not not_26 (not_26_out, not_25_out);
  not not_27 (not_27_out, nor_10_out);
  nor nor_10 (nor_10_out, nand_13_out, nor_9_out);
  not not_28 (not_28_out, xor_1_out);
  xor xor_1 (xor_1_out, nand_14_out, nand_15_out);
  xor xor_2 (xor_2_out, nand_16_out, nand_17_out);
  not not_29 (not_29_out, xor_2_out);
  not not_30 (not_30_out, xor_3_out);
  xor xor_3 (xor_3_out, nand_18_out, nand_19_out);
  xor xor_4 (xor_4_out, nand_20_out, not_26_out);
  not not_31 (not_31_out, xor_4_out);
  not not_32 (C4, not_27_out);
  not not_33 (Z4, not_28_out);
  not not_34 (Z3, not_29_out);
  not not_35 (Z2, not_30_out);
  not not_36 (Z1, not_31_out);
endmodule

module _74373 (
  input  VCC,
  input  GND,
  input  nOE,
  input  LE,
  input  D0,
  input  D1,
  input  D2,
  input  D3,
  input  D4,
  input  D5,
  input  D6,
  input  D7,
  output Q0,
  output Q1,
  output Q2,
  output Q3,
  output Q4,
  output Q5,
  output Q6,
  output Q7
);

  wire buffer_1_out, buffer_2_out, dlatch_1_nq, dlatch_2_nq, dlatch_3_nq, dlatch_4_nq, dlatch_5_nq,
       dlatch_6_nq, dlatch_7_nq, dlatch_8_nq, not_1_out, not_2_out, not_3_out, not_4_out, not_5_out,
       not_6_out, not_7_out, not_8_out, not_9_out;

  buf buffer_1 (buffer_1_out, not_1_out);
  not not_1 (not_1_out, nOE);
  buf buffer_2 (buffer_2_out, LE);
  Dlatch dlatch_1 (.D(D0), .LE(buffer_2_out), .nQ(dlatch_1_nq));  // open: Q
  Dlatch dlatch_2 (.D(D1), .LE(buffer_2_out), .nQ(dlatch_2_nq));  // open: Q
  Dlatch dlatch_3 (.D(D2), .LE(buffer_2_out), .nQ(dlatch_3_nq));  // open: Q
  Dlatch dlatch_4 (.D(D3), .LE(buffer_2_out), .nQ(dlatch_4_nq));  // open: Q
  Dlatch dlatch_5 (.D(D4), .LE(buffer_2_out), .nQ(dlatch_5_nq));  // open: Q
  Dlatch dlatch_6 (.D(D5), .LE(buffer_2_out), .nQ(dlatch_6_nq));  // open: Q
  Dlatch dlatch_7 (.D(D6), .LE(buffer_2_out), .nQ(dlatch_7_nq));  // open: Q
  Dlatch dlatch_8 (.D(D7), .LE(buffer_2_out), .nQ(dlatch_8_nq));  // open: Q
  assign Q0 = buffer_1_out ? not_2_out : 1'bz;  // Controlled_Buffer controlled_buffer_1
  not not_2 (not_2_out, dlatch_1_nq);
  not not_3 (not_3_out, dlatch_2_nq);
  assign Q1 = buffer_1_out ? not_3_out : 1'bz;  // Controlled_Buffer controlled_buffer_2
  not not_4 (not_4_out, dlatch_3_nq);
  assign Q2 = buffer_1_out ? not_4_out : 1'bz;  // Controlled_Buffer controlled_buffer_3
  assign Q3 = buffer_1_out ? not_5_out : 1'bz;  // Controlled_Buffer controlled_buffer_4
  not not_5 (not_5_out, dlatch_4_nq);
  not not_6 (not_6_out, dlatch_5_nq);
  assign Q4 = buffer_1_out ? not_6_out : 1'bz;  // Controlled_Buffer controlled_buffer_5
  not not_7 (not_7_out, dlatch_6_nq);
  assign Q5 = buffer_1_out ? not_7_out : 1'bz;  // Controlled_Buffer controlled_buffer_6
  assign Q6 = buffer_1_out ? not_8_out : 1'bz;  // Controlled_Buffer controlled_buffer_7
  not not_8 (not_8_out, dlatch_7_nq);
  assign Q7 = buffer_1_out ? not_9_out : 1'bz;  // Controlled_Buffer controlled_buffer_8
  not not_9 (not_9_out, dlatch_8_nq);
endmodule

module _4012 (
  input  VSS,
  input  _1A,
  input  _2A,
  input  _4B,
  input  _3A,
  input  _3B,
  input  _4A,
  input  _2B,
  input  NC,
  input  _1B,
  input  GND,
  input  NC_2,
  output _0A,
  output _0B
);

  nand nand_1 (_0A, _1A, _2A, _3A, _4A);
  nand nand_2 (_0B, _1B, _2B, _3B, _4B);
endmodule

module _4030 (
  input  A1,
  input  Vdd,
  input  B1,
  input  A4,
  input  B4,
  input  B2,
  input  A2,
  input  B3,
  input  Vss,
  input  A3,
  output X1,
  output X2,
  output X4,
  output X3
);

  xor xor_1 (X1, B1, A1);
  xor xor_2 (X2, B2, A2);
  xor xor_3 (X4, A4, B4);
  xor xor_4 (X3, A3, B3);
endmodule

module _4040 (
  input  VCC,
  input  GND,
  input  nCLK,
  input  CLR,
  output Q1,
  output Q2,
  output Q3,
  output Q4,
  output Q5,
  output Q6,
  output Q12,
  output Q11,
  output Q10,
  output Q9,
  output Q8,
  output Q7
);

  wire counter_1_q, counter_2_q, counter_3_q, counter_4_q, counter_5_q, counter_6_q, counter_7_q,
       counter_8_q, counter_9_q, counter_10_q, counter_11_q, counter_12_q, not_1_out, not_3_out, not_4_out,
       not_7_out, not_8_out, not_11_out, not_12_out, not_15_out, not_16_out, not_19_out, not_20_out,
       not_23_out, not_24_out;

  not not_1 (not_1_out, nCLK);
  not not_2 (Q1, not_3_out);
  not not_3 (not_3_out, counter_1_q);
  Counter #(.width(1), .max('h1)) counter_1 (
    .D(not_3_out), .Q(counter_1_q), .clk(not_1_out), .clr(CLR));  // open: load, count, carry
  Counter #(.width(1), .max('h1)) counter_2 (
    .D(not_4_out), .Q(counter_2_q), .clk(not_8_out), .clr(CLR));  // open: load, count, carry
  not not_4 (not_4_out, counter_2_q);
  not not_5 (Q12, not_4_out);
  not not_6 (Q2, not_7_out);
  not not_7 (not_7_out, counter_3_q);
  Counter #(.width(1), .max('h1)) counter_3 (
    .D(not_7_out), .Q(counter_3_q), .clk(not_3_out), .clr(CLR));  // open: load, count, carry
  Counter #(.width(1), .max('h1)) counter_4 (
    .D(not_8_out), .Q(counter_4_q), .clk(not_12_out), .clr(CLR));  // open: load, count, carry
  not not_8 (not_8_out, counter_4_q);
  not not_9 (Q11, not_8_out);
  not not_10 (Q3, not_11_out);
  not not_11 (not_11_out, counter_5_q);
  Counter #(.width(1), .max('h1)) counter_5 (
    .D(not_11_out), .Q(counter_5_q), .clk(not_7_out), .clr(CLR));  // open: load, count, carry
  Counter #(.width(1), .max('h1)) counter_6 (
    .D(not_12_out), .Q(counter_6_q), .clk(not_16_out), .clr(CLR));  // open: load, count, carry
  not not_12 (not_12_out, counter_6_q);
  not not_13 (Q10, not_12_out);
  not not_14 (Q4, not_15_out);
  not not_15 (not_15_out, counter_7_q);
  Counter #(.width(1), .max('h1)) counter_7 (
    .D(not_15_out), .Q(counter_7_q), .clk(not_11_out), .clr(CLR));  // open: load, count, carry
  Counter #(.width(1), .max('h1)) counter_8 (
    .D(not_16_out), .Q(counter_8_q), .clk(not_20_out), .clr(CLR));  // open: load, count, carry
  not not_16 (not_16_out, counter_8_q);
  not not_17 (Q9, not_16_out);
  Counter #(.width(1), .max('h1)) counter_9 (
    .D(not_19_out), .Q(counter_9_q), .clk(not_15_out), .clr(CLR));  // open: load, count, carry
  not not_18 (Q5, not_19_out);
  not not_19 (not_19_out, counter_9_q);
  Counter #(.width(1), .max('h1)) counter_10 (
    .D(not_23_out), .Q(counter_10_q), .clk(not_19_out), .clr(CLR));  // open: load, count, carry
  Counter #(.width(1), .max('h1)) counter_11 (
    .D(not_20_out), .Q(counter_11_q), .clk(not_24_out), .clr(CLR));  // open: load, count, carry
  not not_20 (not_20_out, counter_11_q);
  not not_21 (Q8, not_20_out);
  not not_22 (Q6, not_23_out);
  not not_23 (not_23_out, counter_10_q);
  Counter #(.width(1), .max('h1)) counter_12 (
    .D(not_24_out), .Q(counter_12_q), .clk(not_23_out), .clr(CLR));  // open: load, count, carry
  not not_24 (not_24_out, counter_12_q);
  not not_25 (Q7, not_24_out);
endmodule

module Dlatch (
  input  D,
  input  LE,
  output Q,
  output nQ
);

  wire nand_1_out, nand_2_out, not_1_out;

  nand nand_1 (nand_1_out, D, LE);
  not not_1 (not_1_out, D);
  nand nand_2 (nand_2_out, not_1_out, LE);
  nand nand_3 (Q, nand_1_out, nQ);
  nand nand_4 (nQ, Q, nand_2_out);
endmodule
